# Fritzing sketch PyPiBot (saved by Fritzing 0.9.2b)
breadboards: 3

parts:
  Raspberry_Pi1 = Raspberry Pi B+
  MD03A1 = Dual VNH2SP30 Motor Driver [part_number=MD03A]
  VCC1 = 4 x AAA Battery Mount
  IC1 = Voltage Regulator [package=to-220-alt]
  Bauteil1 = SRF05 Ultrasonic Rangefinder
  R1 = Resistor [tolerance=±5% resistance=220 package="0805 [SMD]"]  # not connected
  R2 = Resistor [tolerance=±5% resistance=220 package="0805 [SMD]"]
  DC_Mot_Enc1 = DC Motor with two-phase hall-encoder [part_number=VT-E-G25A-06-177E]
  DC_Mot_Enc2 = DC Motor with two-phase hall-encoder [part_number=VT-E-G25A-06-177E]
  DC_Mot_Enc3 = DC Motor with two-phase hall-encoder [part_number=VT-E-G25A-06-177E]
  DC_Mot_Enc4 = DC Motor with two-phase hall-encoder [part_number=VT-E-G25A-06-177E]
  MD03A2 = Dual VNH2SP30 Motor Driver [part_number=MD03A]

nets:
  N1: Raspberry_Pi1.3v3, DC_Mot_Enc1.pin5, DC_Mot_Enc2.pin5, DC_Mot_Enc3.pin5, DC_Mot_Enc4.pin5
  N2: Raspberry_Pi1.GND, DC_Mot_Enc1.pin2, DC_Mot_Enc2.pin2, DC_Mot_Enc3.pin2, DC_Mot_Enc4.pin2
  N3: MD03A1.1INa, MD03A1.2INb#143
  N4: MD03A1.1INb, MD03A1.2INb#142
  N5: MD03A1.OUT_1A, DC_Mot_Enc1.pin1
  N6: MD03A1.OUT_1B, DC_Mot_Enc1.pin6
  N7: MD03A1.OUT_2A, DC_Mot_Enc3.pin1
  N8: MD03A1.OUT_2B, DC_Mot_Enc3.pin6
  VIN: MD03A1.VIN, VCC1.+, MD03A2.VIN
  GND: MD03A1.GND, VCC1.-, MD03A2.GND
  N9: IC1.IN, Bauteil1.GND, R2.Pin_1
  N10: IC1.OUT, Bauteil1.VCC
  N11: DC_Mot_Enc2.pin1, MD03A2.OUT_2A
  N12: DC_Mot_Enc2.pin6, MD03A2.OUT_2B
  N13: DC_Mot_Enc4.pin1, MD03A2.OUT_1A
  N14: DC_Mot_Enc4.pin6, MD03A2.OUT_1B
  N15: MD03A2.1INa, MD03A2.2INb#142
  N16: MD03A2.1INb, MD03A2.2INb#143
